# Fritzing sketch week02. (saved by Fritzing 0.9.8b)
breadboards: 1

parts:
  元件2 = Arduino Ethernet Shield (Rev3)  # not connected
  R1 = Resistor [tolerance=±5% power=0.25 resistance=220 package=THT]
  R2 = Resistor [tolerance=±5% power=0.25 resistance=220 package=THT]
  R3 = Resistor [tolerance=±5% power=0.25 resistance=220 package=THT]
  S1 = Pushbutton [package="[THT]"]
  S2 = Pushbutton [package="[THT]"]
  S3 = Pushbutton [package="[THT]"]
  LED1 = LED - 5mm [color="Red (633nm)" current=0.030 package="5 mm [THT]"]
  LED2 = LED - 5mm [color="Yellow (592nm)" current=0.030 package="5 mm [THT]"]
  LED3 = LED - 5mm [color="Blue (430nm)" current=0.030 package="5 mm [THT]"]

nets:
  N1: R1.Pin_0, LED1.anode
  N2: R1.Pin_1, S2.Pin_3, S2.Pin_4
  N3: R2.Pin_0, LED3.anode
  N4: R2.Pin_1, S3.Pin_3, S3.Pin_4
  N5: R3.Pin_0, LED2.anode
  N6: R3.Pin_1, S1.Pin_3, S1.Pin_4
  N7: S1.Pin_1, S1.Pin_2, S2.Pin_1, S2.Pin_2, S3.Pin_1, S3.Pin_2
  N8: LED1.cathode, LED2.cathode, LED3.cathode
