# Fritzing sketch week11 (saved by Fritzing 0.9.8b)
breadboards: 1

parts:
  元件1 = 24 NeoPixel Ring [part_number=1586]
  U1 = NodeMCU V1.0
  R1 = Rotary Potentiometer (Small) [maximum_resistance=100kΩ package=THT]

nets:
  N1: 元件1.IN, U1.D2
  VDD: 元件1.VDD, U1.Vin
  GND: 元件1.GND, U1.GND, R1.leg1
  N2: U1.3V3, R1.leg2
  N3: U1.A0, R1.wiper

custom parts:
  24 NeoPixel Ring: 24 ultra bright smart LED NeoPixels are arranged in a circle with 2.6" (66mm) outer diameter. The rings are 'chainable' - connect the output pin of one to the input pin of another. Use only one microcontroller pin to control as many as you can chain together! Each LED is addressable as the driver chip is inside the LED. Each one has ~18mA constant current drive so the color will be very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
  NodeMCU V1.0: ESP8266 based NodeMCU
