# Fritzing sketch week03. (saved by Fritzing 0.9.8b)
breadboards: 1

parts:
  元件1 = Arduino Uno (Rev3)
  LED1 = LED - 5mm [color="Red (633nm)" current=0.030 package="5 mm [THT]"]
  LED2 = LED - 5mm [color="Red (633nm)" current=0.030 package="5 mm [THT]"]
  R1 = Resistor [tolerance=±5% power=0.25 resistance=220 package=THT]
  R2 = Resistor [tolerance=±5% power=0.25 resistance=220 package=THT]
  S1 = Pushbutton [package="[THT]"]
  R3 = Resistor [tolerance=±5% power=0.25 resistance=220 package=THT]

nets:
  N1: 元件1.D13/SCK, R1.Pin_1
  N2: 元件1.GND, LED1.cathode, LED2.cathode, R3.Pin_1
  N3: 元件1.D2, S1.Pin_1, S1.Pin_2, R3.Pin_0
  N4: 元件1.5V, S1.Pin_3, S1.Pin_4
  N5: LED1.anode, R2.Pin_0
  N6: LED2.anode, R1.Pin_0
