# Fritzing sketch week5 (saved by Fritzing 0.9.8b)
breadboards: 1

parts:
  元件1 = Arduino Uno (Rev3)
  LED1 = LED - 5mm [color="Red (633nm)" current=0.030 package="5 mm [THT]"]
  LED2 = LED - 5mm [color="Red (633nm)" current=0.030 package="5 mm [THT]"]
  LED3 = LED - 5mm [color="Red (633nm)" current=0.030 package="5 mm [THT]"]
  LED4 = LED - 5mm [color="Red (633nm)" current=0.030 package="5 mm [THT]"]
  LED5 = LED - 5mm [color="Red (633nm)" current=0.030 package="5 mm [THT]"]
  R1 = Resistor [tolerance=±5% power=0.25 resistance=220 package=THT]
  R5 = Resistor [tolerance=±5% power=0.25 resistance=220 package=THT]
  HC-SR04_Sensor_1 = HC-SR04 Ultrasonic Distance Sensor
  R6 = Resistor [tolerance=±5% power=0.25 resistance=220 package=THT]
  R7 = Resistor [tolerance=±5% power=0.25 resistance=220 package=THT]
  R8 = Resistor [tolerance=±5% power=0.25 resistance=220 package=THT]

nets:
  N1: 元件1.D9_PWM, LED2.anode
  N2: 元件1.D10_PWM/SS, LED3.anode
  N3: 元件1.D11_PWM/MOSI, LED1.anode
  N4: 元件1.D12/MISO, LED4.anode
  N5: 元件1.D13/SCK, LED5.anode
  N6: 元件1.D2, HC-SR04_Sensor_1.ECHO
  N7: 元件1.D3_PWM, HC-SR04_Sensor_1.TRIG
  5V: 元件1.5V, HC-SR04_Sensor_1.VCC
  GND: 元件1.GND, R1.Pin_1, R5.Pin_1, HC-SR04_Sensor_1.GND, R6.Pin_1, R7.Pin_1, R8.Pin_1
  N8: LED1.cathode, R5.Pin_0
  N9: LED2.cathode, R1.Pin_0
  N10: LED3.cathode, R6.Pin_0
  N11: LED4.cathode, R7.Pin_0
  N12: LED5.cathode, R8.Pin_0
