# Fritzing sketch week06 (saved by Fritzing 0.9.8b)
breadboards: 1

parts:
  元件1 = Arduino Uno (Rev3)
  U2 = 74HC4052 [package=dil16]

nets:
  N1: 元件1.A0, U2.Y
  N2: 元件1.D9_PWM, U2.B
  N3: 元件1.D10_PWM/SS, U2.A
  N4: 元件1.D11_PWM/MOSI, U2.X3
  5V: 元件1.5V, U2.VCC
  GND: 元件1.GND, U2.INH, U2.VEE, U2.GND
