# Fritzing sketch Week 8.  (saved by Fritzing 0.9.8b)
circuit board: 14.6543cm x 10.3579cm
breadboards: 1

parts:
  Part1 = Arduino Uno (Rev3)
  R1 = Resistor [tolerance=±5% power=0.25 resistance=220 package=THT]
  R2 = Resistor [tolerance=±5% power=0.25 resistance=220 package=THT]
  R3 = Resistor [tolerance=±5% power=0.25 resistance=220 package=THT]
  R4 = Resistor [tolerance=±5% power=0.25 resistance=220 package=THT]
  R5 = Resistor [tolerance=±5% power=0.25 resistance=220 package=THT]
  R6 = Resistor [tolerance=±5% power=0.25 resistance=220 package=THT]
  R7 = Resistor [tolerance=±5% power=0.25 resistance=220 package=THT]
  R8 = Resistor [tolerance=±5% power=0.25 resistance=220 package=THT]
  S1 = Momentary Switch [package=ksa_sealed_tac_switch]
  S2 = Momentary Switch [package=ksa_sealed_tac_switch]
  o1 = Module display OLED I2C 128x64 SSD1306 [package=THT]
  LED1 = LED - 5mm [color="Red (633nm)" current=0.030 package="5 mm [THT]"]
  LED2 = LED - 5mm [color="Red (633nm)" current=0.030 package="5 mm [THT]"]
  LED3 = LED - 5mm [color="Red (633nm)" current=0.030 package="5 mm [THT]"]
  LED4 = LED - 5mm [color="Red (633nm)" current=0.030 package="5 mm [THT]"]
  LED5 = LED - 5mm [color="Red (633nm)" current=0.030 package="5 mm [THT]"]
  LED6 = LED - 5mm [color="Red (633nm)" current=0.030 package="5 mm [THT]"]
  LED7 = LED - 5mm [color="Red (633nm)" current=0.030 package="5 mm [THT]"]
  LED8 = LED - 5mm [color="Red (633nm)" current=0.030 package="5 mm [THT]"]
  R9 = Rotary Potentiometer (Small) [maximum_resistance=100kΩ package=THT]
  IC1 = IC, DIP package, 16 pins [chip_label=4051]
  IC2 = IC, DIP package, 16 pins [chip_label=4051]
  Part2 = Thumb Joystick
  R10 = Resistor [tolerance=±5% power=0.25 resistance=10k package=THT]
  R11 = Resistor [tolerance=±5% power=0.25 resistance=10k package=THT]
  Part3 = Thumb Joystick

nets:
  N1: Part1.A0, IC2.pin3
  N2: Part1.A4/SDA, o1.SDA
  N3: Part1.A5/SCL, o1.SCL
  N4: Part1.D8, IC2.pin10
  N5: Part1.D9_PWM, IC2.pin11
  N6: Part1.D10_PWM/SS, IC1.pin9
  N7: Part1.D11_PWM/MOSI, IC1.pin10
  N8: Part1.D12/MISO, IC1.pin11
  N9: Part1.D2, S1.1
  N10: Part1.D3_PWM, S2.1
  N11: Part1.D5_PWM, Part3.SEL
  N12: Part1.D6_PWM, Part2.SEL
  N13: Part1.D7, IC2.pin9
  VCC: Part1.5V, S1.4, S2.2, o1.VCC, R9.leg1, IC1.pin3, IC1.pin16, IC2.pin16, Part2.VCC
  GND: Part1.GND, o1.GND, LED1.cathode, LED2.cathode, LED3.cathode, LED4.cathode, LED5.cathode, LED6.cathode, LED7.cathode, LED8.cathode, R9.leg2, IC1.pin6, IC1.pin7, IC1.pin8, IC2.pin6, IC2.pin7, IC2.pin8, Part2.GND, R10.Pin_0, R11.Pin_0
  N14: R1.Pin_0, LED1.anode
  N15: R1.Pin_1, IC1.pin4
  N16: R2.Pin_0, LED5.anode
  N17: R2.Pin_1, IC1.pin12
  N18: R3.Pin_1, IC1.pin2
  N19: R4.Pin_0, LED6.anode
  N20: R4.Pin_1, IC1.pin15
  N21: R5.Pin_0, LED3.anode
  N22: R5.Pin_1, IC1.pin5
  N23: R6.Pin_0, LED7.anode
  N24: R6.Pin_1, IC1.pin14
  N25: R7.Pin_0, LED4.anode
  N26: R7.Pin_1, IC1.pin1
  N27: R8.Pin_0, LED8.anode
  N28: R8.Pin_1, IC1.pin13
  N29: S1.2, R11.Pin_1
  N30: S2.4, R10.Pin_1
  N31: R9.wiper, IC2.pin13
  N32: IC2.pin1, Part3.HORZ
  N33: IC2.pin12, Part3.VERT
  N34: IC2.pin14, Part2.VERT
  N35: IC2.pin15, Part2.HORZ

custom parts:
  Module display OLED I2C 128x64 SSD1306: Ecran OLED I2C SSD163 de 128x64 avec connexion I2C
