# Fritzing sketch week07 (saved by Fritzing 0.9.8b)
circuit board: 10.2801cm x 7.13405cm

parts:
  KEYPAD1 = Membrane Matrix Keypad
  元件1 = Arduino Uno (Rev3)

nets:
  N1: KEYPAD1.1, 元件1.D9_PWM
  N2: KEYPAD1.2, 元件1.D8
  N3: KEYPAD1.3, 元件1.D7
  N4: KEYPAD1.4, 元件1.D6_PWM
  N5: KEYPAD1.5, 元件1.D5_PWM
  N6: KEYPAD1.6, 元件1.D4
  N7: KEYPAD1.7, 元件1.D3_PWM

custom parts:
  Membrane Matrix Keypad: Membrane Matrix 3x4 Keypad
